# Fritzing sketch Gateway_fritzing (saved by Fritzing 1.0.1rc)

parts:
  LoRa_Module1 = Ra-01 - LoRa Module SX1278 [part_number=SX1278]
  L1 = Inductor [package="400 mil [THT]"]
  A2 = Arduino UNO R4 WiFi

nets:
  N1: LoRa_Module1.GND, A2.Pin_48
  N2: LoRa_Module1.NSS, A2.Pin_44
  N3: LoRa_Module1.MOSI, A2.Pin_45
  N4: LoRa_Module1.MISO, A2.Pin_46
  N5: LoRa_Module1.SCK, A2.Pin_47
  N6: LoRa_Module1.ANT, L1.pin_0
  N7: LoRa_Module1.3.3V, A2.Pin_7
  N8: LoRa_Module1.RESET, A2.Pin_43
  N9: LoRa_Module1.DIO0, A2.Pin_36

notes:
  SCK
  MISO
  MOSI
  NSS
  GND
  ANT
  DIO0
  3.3V
  RESET
  LoRa
  Created by 3D Printer

custom parts:
  Ra-01 - LoRa Module SX1278: The Ra-01 LoRa Module featuring the SX1278 engine by Semtech. Module by AI-Thinker. Module (Ra-01) specifications from: https://www.banggood.com/Ra-01-Smart-Electronics-SX1278-LoRa-Spread-Spectrum-Wireless-Module-Ultra-Far-10KM-433M-p-1130769.html Description: Power supply: DC1.8-3.7V(3.3V) Chip: SX1278 Frequency: 433Mhz Operating temperature: -40~+85°C On Sheild Description (may vary by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
  Arduino UNO R4 WiFi: The Arduino UNO R4 WiFi merges the RA4M1 microprocessor from Renesas with the ESP32-S3 from Espressif, creating an all-in-one tool for makers with enhanced processing power and a diverse array of new peripherals.
