# Fritzing sketch Station1_fritzing_gateway (saved by Fritzing 1.0.1rc)
breadboards: 1

parts:
  A1 = Arduino R4 Minima
  Part1 = Adafruit BME680 [part_number="Adafruit #3660"]
  LoRa_Module1 = Ra-01 - LoRa Module SX1278 [part_number=SX1278]
  Sensor1 = Gas Sensor Breakout Board
  L1 = Inductor [package="400 mil [THT]"]
  R1 = Photocell (LDR) [package=THT]
  R2 = Resistor [tolerance=±5% power=0.25 resistance=10k package=THT]
  R3 = Resistor [tolerance=±5% power=0.25 resistance=220 package=THT]  # not connected
  LED1 = LED - 5mm [color="Red (633nm)" current=0.030 package="5 mm [THT]"]  # not connected
  LED2 = LED - 5mm [color="Orange (620nm)" current=0.030 package="5 mm [THT]"]  # not connected
  LED3 = LED - 5mm [color="Green (570nm)" current=0.030 package="5 mm [THT]"]  # not connected
  R4 = Resistor [tolerance=±5% power=0.25 resistance=220 package=THT]  # not connected
  R5 = Resistor [tolerance=±5% power=0.25 resistance=220 package=THT]

nets:
  N1: A1.Pin_4, LoRa_Module1.3.3V
  VCC: A1.Pin_5, Part1.VCC, Sensor1.5V, R1.pin_0
  GND: A1.Pin_6, A1.Pin_17, A1.Pin_28, Part1.GND, LoRa_Module1.GND, Sensor1.GND, R2.Pin_0, R5.Pin_0
  N2: A1.Pin_9, Sensor1.AOUT
  N3: A1.Pin_10, R1.pin_1, R2.Pin_1
  N4: A1.Pin_13, Part1.SDI/SDA
  N5: A1.Pin_14, Part1.SCK/SCL
  N6: A1.Pin_33, LoRa_Module1.DIO0
  N7: A1.Pin_40, LoRa_Module1.RESET
  N8: A1.Pin_41, LoRa_Module1.NSS
  N9: A1.Pin_42, LoRa_Module1.MOSI
  N10: A1.Pin_43, LoRa_Module1.MISO
  N11: A1.Pin_44, LoRa_Module1.SCK
  N12: LoRa_Module1.ANT, L1.pin_0

notes:
  SCK
  MISO
  MOSI
  NSS
  GND
  ANT
  DIO0
  3.3V
  RESET
  5V
  Aout
  SDA
  SCL
  10K
  LDR
  220Ω
  LoRa
  MQ-135
  BME680
  Created by 3D Printer

custom parts:
  Arduino R4 Minima: Introducing the Arduino UNO R4 Minima! This board boasts the RA4M1 microprocessor from Renesas, delivering increased processing power, expanded memory, and additional peripherals.
  Ra-01 - LoRa Module SX1278: The Ra-01 LoRa Module featuring the SX1278 engine by Semtech. Module by AI-Thinker. Module (Ra-01) specifications from: https://www.banggood.com/Ra-01-Smart-Electronics-SX1278-LoRa-Spread-Spectrum-Wireless-Module-Ultra-Far-10KM-433M-p-1130769.html Description: Power supply: DC1.8-3.7V(3.3V) Chip: SX1278 Frequency: 433Mhz Operating temperature: -40~+85°C On Sheild Description (may vary by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
  Gas Sensor Breakout Board: Gas sensor breakout board. Input voltage is 5V. Sensor output is available in analog and digital.
